# Fritzing sketch circuit (saved by Fritzing 0.9.3b)
breadboards: 1

parts:
  Part1 = Arduino Uno (Rev3)
  Part2 = Arduino Uno (Rev3)
  U1 = Vibration Motor- ROB-08449 [package=vibe-motor-10mm]
  J1 = Basic Force Sensing Resistor (FSR) [package=THT]
  R1 = Resistor [tolerance=±5% resistance=10k package=THT]
  hc-sr1 = hc-sr04

nets:
  N1: Part1.D6_PWM, U1.-
  N2: Part1.GND, U1.+
  N3: Part2.A0, J1.pin_1, R1.Pin_0
  N4: Part2.D12/MISO, hc-sr1.Echo
  N5: Part2.D13/SCK, hc-sr1.Trig
  5V: Part2.5V, J1.pin_0, hc-sr1.VCC
  GND: Part2.GND, R1.Pin_1, hc-sr1.GND
